# Fritzing sketch MysteryMachine2 (saved by Fritzing 0.8.7b)
breadboards: 3

parts:
  Onderdeel1 = Arduino Uno (Rev3)
  RotSwitch1 = female pin header, 6 pins [form="♀ (female)"]
  R1 = Resistor [tolerance=±5% resistance=1k package=THT]
  R2 = Resistor [tolerance=±5% resistance=1k package=THT]
  LED8 = LED - 5mm [color="Red (633nm)" package="5 mm [THT]"]
  LED9 = LED - 5mm [color="Orange (612nm)" package="5 mm [THT]"]
  LED10 = LED - 5mm [color="Yellow (585nm)" package="5 mm [THT]"]
  LED11 = LED - 5mm [color="Green (565nm)" package="5 mm [THT]"]
  LED12 = LED - 5mm [color="Blue (505nm)" package="5 mm [THT]"]
  R3 = Resistor [tolerance=±5% resistance=1k package=THT]
  R4 = Resistor [tolerance=±5% resistance=1k package=THT]
  R5 = Resistor [tolerance=±5% resistance=1k package=THT]
  R6 = Resistor [tolerance=±5% resistance=1k package=THT]
  R7 = Resistor [tolerance=±5% resistance=1k package=THT]
  R8 = Resistor [tolerance=±5% resistance=1k package=THT]
  R9 = Resistor [tolerance=±5% resistance=1k package=THT]
  R10 = Resistor [tolerance=±5% resistance=1k package=THT]
  LED13 = LED - 5mm [color="Red (633nm)" package="5 mm [THT]"]
  RotSwitch2 = female pin header, 6 pins [form="♀ (female)"]
  R11 = Resistor [tolerance=±5% resistance=1k package=THT]
  R12 = Resistor [tolerance=±5% resistance=1k package=THT]
  R14 = Resistor [tolerance=±5% resistance=1k package=THT]
  R15 = Resistor [tolerance=±5% resistance=1k package=THT]
  R16 = Resistor [tolerance=±5% resistance=1k package=THT]
  R17 = Resistor [tolerance=±5% resistance=1k package=THT]
  R18 = Resistor [tolerance=±5% resistance=1k package=THT]
  LED14 = LED - 5mm [color="Orange (612nm)" package="5 mm [THT]"]
  LED15 = LED - 5mm [color="Green (565nm)" package="5 mm [THT]"]
  LED16 = LED - 5mm [color="Yellow (585nm)" package="5 mm [THT]"]
  LED17 = LED - 5mm [color="Blue (505nm)" package="5 mm [THT]"]
  S1 = Pushbutton [package="[THT]"]
  LED18 = LED - 5mm [color="Red (633nm)" package="5 mm [THT]"]
  LED19 = LED - 5mm [color="Green (555nm)" package="5 mm [THT]"]
  LED20 = LED - 5mm [color="Blue (430nm)" package="5 mm [THT]"]
  R21 = Resistor [tolerance=±5% resistance=1k package=THT]
  U1 = SPDT Slide Switch [package=ayz0202]
  R23 = Resistor [tolerance=±5% resistance=1k package=THT]

nets:
  N1: Onderdeel1.A0, S1.Pin_3, S1.Pin_4, R23.Pin_0
  N2: Onderdeel1.D8, RotSwitch1.pin5, LED12.cathode, R4.Pin_0
  N3: Onderdeel1.D9_PWM, RotSwitch1.pin4, LED11.cathode, R6.Pin_0
  N4: Onderdeel1.D10_PWM/SS, RotSwitch1.pin3, LED10.cathode, R5.Pin_0
  N5: Onderdeel1.D11_PWM/MOSI, RotSwitch1.pin2, LED9.cathode, R3.Pin_0
  N6: Onderdeel1.D12/MISO, RotSwitch1.pin1, R2.Pin_0, LED8.cathode
  N7: Onderdeel1.D0/RX, RotSwitch2.pin4, LED15.cathode
  N8: Onderdeel1.D1/TX, RotSwitch2.pin3, R18.Pin_0
  N9: Onderdeel1.D2, LED13.cathode, RotSwitch2.pin1, R17.Pin_0
  N10: Onderdeel1.D3_PWM, RotSwitch2.pin2, LED14.cathode
  N11: Onderdeel1.D4, RotSwitch2.pin5, LED17.cathode
  N12: Onderdeel1.D5_PWM, LED20.cathode
  N13: Onderdeel1.D6_PWM, LED19.cathode
  N14: Onderdeel1.D7, LED18.cathode
  N15: Onderdeel1.5V, RotSwitch1.pin6, RotSwitch2.pin6, LED16.cathode, S1.Pin_1, S1.Pin_2, U1.1, U1.6
  N16: Onderdeel1.GND, R1.Pin_1, R2.Pin_1, R3.Pin_1, R5.Pin_1, R6.Pin_1, R7.Pin_1, R8.Pin_1, R9.Pin_1, R10.Pin_1
  N17: R1.Pin_0, LED8.anode
  N18: LED9.anode, R7.Pin_0
  N19: LED10.anode, R8.Pin_0
  N20: LED11.anode, R9.Pin_0
  N21: LED12.anode, R10.Pin_0
  N22: LED13.anode, R16.Pin_0
  N23: R11.Pin_0, LED14.anode
  N24: R11.Pin_1, R12.Pin_1, R14.Pin_1, R15.Pin_1, R16.Pin_1, R17.Pin_1, R18.Pin_1, R21.Pin_1, R23.Pin_1
  N25: R12.Pin_0, LED15.anode
  N26: R14.Pin_0, LED16.anode
  N27: R15.Pin_0, LED17.anode
  N28: LED18.anode, LED19.anode, LED20.anode, R21.Pin_0
  N29: U1.3, U1.4
  N30: U1.2, U1.5
